// Logisim project dicksingh.circ as structural Verilog: 3 circuits, main circuit main
module main (
  input  [7:0] in_1,
  output [7:0] out_2,
  output [7:0] out_3,
  output [7:0] out_4
);

  wire alu_1_p3;

  pc pc_1 ();  // open: in_1, out_2
  Decoder #(.select(3)) decoder_1 ();  // open: out0, out1, out2, out3, out4, out5, out6, out7, sel, en
  ROM #(.dataWidth(8)) rom_1 ();  // open: addr, data, sel
  Register #(.width(8)) register_1 ();  // open: D, en, Q, clk, clr
  // Sign_Extend sign_extend_1: pin names not known
  Register register_2 ();  // open: D, en, Q, clk, clr
  // ALU_part alu_1: pin names not known; wires that end beside it: out_3, out_4, alu_1_p3
  Clock clock_1 (.out(alu_1_p3));
endmodule

module ALU (
  input  [7:0] in_1,
  input  [7:0] in_2,
  output [7:0] out_3
);

  Adder adder_1 ();  // open: a, b, out, cin, cout
endmodule

module pc (
  input  [7:0] in_1,
  output [7:0] out_2
);

  Adder adder_1 ();  // open: a, b, out, cin, cout
  Register register_1 ();  // open: D, en, Q, clk, clr
endmodule
